# Fritzing sketch Diagram (saved by Fritzing 1.0.5)
breadboards: 1

parts:
  Part1 = Arduino Nano (Rev3.0)
  F1 = Fan - 4 wire [package=THT]
  Part2 = Humidity Temperature Sensor SHT15  # not connected
  KY-1 = Keyes Relay [package=THT]
  KY-2 = Keyes Relay [package=THT]
  Part3 = LCD1602-I2C
  L1 = Bulb holder (E10) with base
  J1 = 120V duplex outlet_1
  VCC1 = Battery block 9V [internal_resistance=0.1Ω]
  RE1 = Rotary Encoder [package=THT]  # not connected

nets:
  GND: Part1.GND, KY-1.ground, KY-2.ground, Part3.GND
  N1: Part1.D2, F1.PWM
  N2: Part1.D3, F1.Tach
  N3: Part1.VIN, KY-1.NC, VCC1.+
  5V: Part1.5V, KY-1.power, KY-2.power, Part3.VCC
  N4: Part1.A5, Part3.SCL
  N5: Part1.A4, Part3.SDA
  N6: F1.GND, VCC1.-
  N7: F1.Power, KY-1.C
  N8: KY-2.NC, L1.pin_1
  N9: KY-2.C, J1.H2
  N10: L1.pin_2, J1.N2

custom parts:
  Fan - 4 wire: Fan, 4 wire with tach.
  Keyes Relay: The Keyes 5V relay module is suitable for SCM development, home appliance control. It uses a 5V~12V TIL control signal which can control DC / AC signal.
  LCD1602-I2C: A standard character display, usually with 2x16 characters. Comes in many colors with LCM1602 IIC attached.
  Bulb holder (E10) with base: A bulb holder for an E10 bulb with a base.
  120V duplex outlet_1: 120V duplex outlet.
